# Fritzing sketch pool-controller (saved by Fritzing 0.9.3b)
circuit board: 5.92561cm x 5.10948cm
breadboards: 1

parts:
  U1 = NodeMCU V1.0
  R1 = Resistor [tolerance=±5% resistance=4.7k package=THT]
  U2 = RF-LINK_TX [package=rf-link_tx]
  DS2 = DS18B20 1-Wire Temperature Sensor Probe Cable

nets:
  N1: U1.D0, U1.RST
  3V3: U1.3V3, R1.Pin_0, DS2.VDD
  GND: U1.GND, U2.GND, DS2.GND
  N2: U1.D7, R1.Pin_1, DS2.DQ
  N3: U1.D8, U2.DATA
  VIN: U1.Vin, U2.+5V

custom parts:
  NodeMCU V1.0: ESP8266 based NodeMCU
